# Fritzing sketch wiring (saved by Fritzing 0.8.3b)
circuit board: 4.17925cm x 4.38385cm
breadboards: 1

parts:
  ATTiny2313 = IC, DIP package, 20 pins [chip_label=IC]
  R200 = Resistor [tolerance=±5% resistance=220 package=THT]
  R1K = Resistor [tolerance=±5% resistance=220 package=THT]
  C0_1u = Ceramic Capacitor [capacitance=100nF package="200 mil [THT, multilayer]"]
  QVR1 = Ceramic Capacitor [capacitance=100nF package="200 mil [THT, multilayer]"]
  Q1 = PNP-Transistor [package="TO92 [THT]"]
  VCC = Battery
  C0_1u_2 = Ceramic Capacitor [capacitance=100nF package="200 mil [THT, multilayer]"]
  PUDDLE = female pin header, 2 pins [form="♀ (female)"]
  ISP = double row male pin header, 6 pins [form="♂ (male)"]
  BUTTON = female pin header, 2 pins [form="♀ (female)"]
  Q2 = PNP-Transistor [package="TO92 [THT]"]
  QVR = Ceramic Capacitor [capacitance=100nF package="200 mil [THT, multilayer]"]
  R330K = Resistor [tolerance=±5% resistance=220 package=THT]
  R330K_2 = Resistor [tolerance=±5% resistance=220 package=THT]
  OUT = female pin header, 2 pins [form="♀ (female)"]

nets:
  N1: ATTiny2313.pin1, ISP.pin3
  N2: ATTiny2313.pin2, BUTTON.pin2
  N3: ATTiny2313.pin3, BUTTON.pin1
  N4: ATTiny2313.pin10, C0_1u.1, QVR1.0, Q1.E, VCC.-, C0_1u_2.0, ISP.pin4, Q2.E, QVR.0, R330K.Pin_1, R330K_2.Pin_1, OUT.pin1
  N5: ATTiny2313.pin14, R200.Pin_1
  N6: ATTiny2313.pin15, R1K.Pin_1
  N7: ATTiny2313.pin16, Q2.C
  N8: ATTiny2313.pin17, ISP.pin5
  N9: ATTiny2313.pin18, ISP.pin1
  N10: ATTiny2313.pin19, ISP.pin2
  N11: ATTiny2313.pin20, C0_1u.0, VCC.+, ISP.pin6
  N12: R200.Pin_0, Q1.B, R330K.Pin_0
  N13: QVR1.1, PUDDLE.pin1
  N14: Q1.C, C0_1u_2.1, Q2.B, R330K_2.Pin_0, OUT.pin2
  N15: PUDDLE.pin2, QVR.1

notes:
  SGD
  DGS
  1
  11
  MISO
  SCK
  /RESE
  VCC
  MOSI
  GND
